# Fritzing sketch midi_hold (saved by Fritzing 0.9.9b)
breadboards: 1

parts:
  RE2 = KY-040 Rotary encoder [package=THT]
  RE1 = KY-040 Rotary encoder [package=THT]
  DIN1 = DIN-5 jack (MIDI) [package=THT]
  Grove2 = Grove 4 Digit Display
  Part1 = Arduino Nano (Rev3.0) (ICSP)
  R2 = Resistor [tolerance=±5% resistance=220 package="0805 [SMD]"]
  R3 = Resistor [tolerance=±5% resistance=220 package="0805 [SMD]"]

nets:
  GND: RE2.GND, DIN1.2, Grove2.GND, Part1.GND
  N1: RE2.Vcc, Part1.D9
  N2: RE2.DT, Part1.D12/MISO
  N3: RE2.CLK, Part1.D11/MOSI
  N4: RE1.GND, Part1.D6
  N5: RE1.Vcc, Part1.D5
  N6: RE1.SW, Part1.D4
  N7: RE1.DT, Part1.D3
  N8: RE1.CLK, Part1.D2
  N9: DIN1.5, R2.Pin_1
  N10: DIN1.4, R3.Pin_1
  5V: Grove2.5V, Part1.5V, R2.Pin_0
  N11: Grove2.DIO, Part1.D8
  N12: Grove2.CLK, Part1.D7
  N13: Part1.D1/TX, R3.Pin_0

custom parts:
  KY-040 Rotary encoder: KY-040 Rotary Encoder with switch on breakout borad from AZ Delivery
  Grove 4 Digit Display: A 4 7-seg display
